# Fritzing sketch sketch (saved by Fritzing 0.9.9b)
breadboards: 1

parts:
  part = MQ-7 breakout
  part_2 = MQ-9 breakout
  part_3 = MQ-3 breakout
  part_4 = ESP32S-HiLetgo

nets:
  VCC: part.VCC, part_2.VCC, part_3.VCC, part_4.VIN
  GND: part.GND, part_2.GND, part_3.GND, part_4.GND
  N1: part.AO, part_4.GPIO32
  N2: part_2.AO, part_4.GPIO34
  N3: part_3.AO, part_4.GPIO33

custom parts:
  MQ-7 breakout: SKU: 101282
  MQ-9 breakout: SKU: 101284
  MQ-3 breakout: Alcohol sensor is capable of detecting alcohol (ethanol) particles on itself and gives the information in digital form back to us to manipulate with it. SKU:101251 • Voltage: 5V DC • Power: max 750mW • Measurement range: 0.04-4mg/L
  ESP32S-HiLetgo: HiLetgo ESP-WROOM-32 ESP32 ESP-32S Development Board 2.4GHz Dual-Mode WiFi + Bluetooth Dual Cores Microcontroller The ESP32 integrated with Antenna switches, RF Balun, power amplifiers, low-noise amplifiers, filters, and management modules, and the entire solution occupies the least area of PCB. 2.4 GHz Wi-Fi plus Bluetooth dual-mode chip, with TSMC Ultra-low power consumption 40nm technology,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
